# Fritzing sketch ascale (saved by Fritzing 0.9.3b)
breadboards: 1

parts:
  Part2 = Arduino Nano (Rev3.0)
  Part3 = HX711 Weighing Sensor Module
  Part4 = Bluetooth HC-05 Macho
  Load_Cell1 = Load Cell - Red/white/black/green

nets:
  N1: Part2.D2, Part3.DO/RX
  N2: Part2.D3, Part3.CK/TX
  N3: Part2.D10, Part4.TXD
  N4: Part2.D11/MOSI, Part4.RXD
  VCC: Part3.VCC, Part4.VCC
  GND: Part3.GND, Part4.GND
  N5: Part3.E+, Load_Cell1.wire1
  N6: Part3.E-, Load_Cell1.wire2
  N7: Part3.A+, Load_Cell1.wire3
  N8: Part3.A-, Load_Cell1.wire4

custom parts:
  Load Cell - Red/white/black/green: A rectangle load cell/weighting pressure Sensor with four wires - Red, white, black, green. Normally corresponding with E+, E-, A+, A- respectively.
